# Fritzing sketch Шаблон электросхемы проекта (saved by Fritzing 0.9.3b)
breadboards: 1

parts:
  VCC1 = Battery
  S1 = Toggle Switch [package=THT]
  S2 = Pushbutton [package="[THT]"]
  S3 = Pushbutton [package="[THT]"]
  S4 = Pushbutton [package="[THT]"]
  S5 = Pushbutton [package="[THT]"]
  S6 = Pushbutton [package="[THT]"]
  S7 = Pushbutton [package="[THT]"]
  S8 = Pushbutton [package="[THT]"]
  S9 = Pushbutton [package="[THT]"]
  S10 = Pushbutton [package="[THT]"]
  R1 = Resistor [tolerance=±5% resistance=220 package=THT]  # not connected
  Disp1 = LBT2088AH [part_number=LBT2088AH]
  Часть1 = Arduino Uno (Rev3)
  SP1 = SPEAKER [package=pcb_mount_speaker]
  Q1 = NPN-Transistor [package="TO92 [THT]"]

nets:
  N1: VCC1.-, S1.L1
  N2: VCC1.+, Disp1.pin_4, Часть1.VIN, Q1.E
  N3: S1.L2, S2.Pin_1, S2.Pin_2, S4.Pin_1, S4.Pin_2, S8.Pin_1, S8.Pin_2, S9.Pin_1, S9.Pin_2, Disp1.pin_3, Часть1.GND, SP1.+
  N4: S2.Pin_3, S2.Pin_4, Часть1.D2
  N5: S3.Pin_1, S3.Pin_2, S5.Pin_1, S5.Pin_2, S7.Pin_1, S7.Pin_2, S10.Pin_1, S10.Pin_2
  N6: S3.Pin_3, S3.Pin_4, Часть1.D5_PWM
  N7: S4.Pin_3, S4.Pin_4, Часть1.D3_PWM
  N8: S5.Pin_3, S5.Pin_4, Часть1.D4
  N9: S6.Pin_1, S6.Pin_2
  N10: S6.Pin_3, S6.Pin_4
  N11: S7.Pin_3, S7.Pin_4, Часть1.D7
  N12: S8.Pin_3, S8.Pin_4, Часть1.D9_PWM
  N13: S9.Pin_3, S9.Pin_4, Часть1.D8
  N14: S10.Pin_3, S10.Pin_4, Часть1.D6_PWM
  N15: Disp1.pin2, Часть1.D10_PWM/SS
  N16: Часть1.D11_PWM/MOSI, Q1.B
  N17: SP1.-, Q1.C
